# Fritzing sketch esquema (saved by Fritzing 0.9.3b)
breadboards: 1

parts:
  Componente1 = Arduino Uno (Rev3)
  LED1 = LED - 5mm [color="Red (633nm)" package="5 mm [THT]"]
  R1 = TRIMPOT [package=3362u-2]

nets:
  N1: Componente1.A0, R1.WIPER
  N2: Componente1.D2, LED1.anode
  N3: Componente1.5V, R1.CCW
  N4: Componente1.GND, LED1.cathode, R1.CW
