# Fritzing sketch esquematico (saved by Fritzing 0.9.3b)
breadboards: 1

parts:
  LED1 = LED - 5mm [color="Red (633nm)" package="5 mm [THT]"]
  R1 = Resistor [tolerance=±5% resistance=1k package="1206 [SMD]"]
  LED2 = LED - 5mm [color="Green (570nm)" package="5 mm [THT]"]
  LED4 = LED - 5mm [color="Blue (525nm)" package="5 mm [THT]"]
  R4 = Resistor [tolerance=±5% resistance=1k package="1206 [SMD]"]
  LED3 = LED - 5mm [color="Yellow (595nm)" package="5 mm [THT]"]
  Componente1 = Arduino Uno (Rev3)
  R5 = Resistor [tolerance=±5% resistance=1k package="1206 [SMD]"]
  R6 = Resistor [tolerance=±5% resistance=1k package="1206 [SMD]"]
  R7 = TRIMPOT [package=trimpot_pth_s3_lock]
  R8 = Resistor [tolerance=±5% resistance=1k package="1206 [SMD]"]
  R9 = Resistor [tolerance=±5% resistance=1k package="1206 [SMD]"]
  R2 = Resistor [tolerance=±5% resistance=1k package="1206 [SMD]"]
  R3 = Resistor [tolerance=±5% resistance=1k package="1206 [SMD]"]
  S5 = SWITCH-MOMENTARY-2 [package=tactile-pth]  # not connected
  S1 = Pushbutton [package="[THT]"]
  S2 = Pushbutton [package="[THT]"]
  S3 = Pushbutton [package="[THT]"]
  S4 = Pushbutton [package="[THT]"]

nets:
  GND: LED1.cathode, LED2.cathode, LED4.cathode, LED3.cathode, Componente1.GND, R5.Pin_1, R6.Pin_1, R7.CW, R8.Pin_1, R9.Pin_1
  N1: LED1.anode, R1.Pin_0
  N2: R1.Pin_1, Componente1.D0/RX
  N3: LED2.anode, R2.Pin_0
  N4: LED4.anode, R4.Pin_0
  N5: R4.Pin_1, Componente1.D3_PWM
  N6: LED3.anode, R3.Pin_0
  N7: Componente1.A5/SCL, R7.WIPER
  N8: Componente1.D8, R8.Pin_0, S4.Pin_1, S4.Pin_2
  N9: Componente1.D9_PWM, R9.Pin_0, S3.Pin_1, S3.Pin_2
  N10: Componente1.D10_PWM/SS, R6.Pin_0, S2.Pin_1, S2.Pin_2
  N11: Componente1.D11_PWM/MOSI, R5.Pin_0, S1.Pin_1, S1.Pin_2
  N12: Componente1.D1/TX, R2.Pin_1
  N13: Componente1.D2, R3.Pin_1
  N14: Componente1.3V3, S1.Pin_3, S1.Pin_4, S2.Pin_3, S2.Pin_4, S3.Pin_3, S3.Pin_4, S4.Pin_3, S4.Pin_4
  N15: Componente1.5V, R7.CCW
